// Digital circuit 4bit_counter.dig as structural Verilog
module _4bit_counter (
  input  CP,
  input  R,
  output QA,
  output QB,
  output QC,
  output QD,
  output CP_2
);

  _74161 _74161_1 (
    .pin1(R), .pin2(CP), .pin3(1'b0), .pin4(1'b0), .pin5(1'b0), .pin6(1'b0), .pin7(1'b1), .pin8(1'b0),
    .pin9(1'b1), .pin10(1'b1), .pin11(QD), .pin12(QC), .pin13(QB), .pin14(QA), .pin15(CP_2), .pin16(1'b1));
endmodule
