// Digital circuit 8bit_shifter.dig as structural Verilog
module _8bit_shifter (
  input  D,
  input  MR,
  input  CP,
  output _7,
  output _6,
  output _5,
  output _4,
  output _3,
  output _2,
  output _1,
  output _0
);

  _74164 _74164_1 (
    .pin1(D), .pin2(D), .pin3(_0), .pin4(_1), .pin5(_2), .pin6(_3), .pin7(1'b0), .pin8(CP), .pin9(MR),
    .pin10(_4), .pin11(_5), .pin12(_6), .pin13(_7), .pin14(1'b1));
endmodule
