// Digital circuit Ksmoth.dig as structural Verilog
module Ksmoth (
  input  KI3,
  input  KI4,
  input  KI2,
  input  KI1,
  input  CP,
  output KO3,
  output KO4,
  output KO2,
  output KO1
);

  D_FF_AS d_ff_as_1 (.Set(KI1), .D(1'b0), .C(CP), .Clr(1'b0), .Q(KO1));  // open: nQ
  D_FF_AS d_ff_as_2 (.Set(KI2), .D(1'b0), .C(CP), .Clr(1'b0), .Q(KO2));  // open: nQ
  D_FF_AS d_ff_as_3 (.Set(KI3), .D(1'b0), .C(CP), .Clr(1'b0), .Q(KO3));  // open: nQ
  D_FF_AS d_ff_as_4 (.Set(KI4), .D(1'b0), .C(CP), .Clr(1'b0), .Q(KO4));  // open: nQ
endmodule
