// Digital circuit determined_fish.dig as structural Verilog
module determined_fish (
  input  clk
);

  wire _8bit_shifter_1__0, _8bit_shifter_1__1, _8bit_shifter_1__2, _8bit_shifter_1__3, _8bit_shifter_1__4,
       _8bit_shifter_1__5, _8bit_shifter_1__6, _8bit_shifter_1__7, _8bit_shifter_2__0, _8bit_shifter_2__1,
       _8bit_shifter_2__2, _8bit_shifter_2__3, _8bit_shifter_2__4, _8bit_shifter_2__5, _8bit_shifter_2__6,
       _8bit_shifter_2__7, _8bit_shifter_3__0, _8bit_shifter_3__1, _8bit_shifter_3__2, _8bit_shifter_3__3,
       _8bit_shifter_3__4, _8bit_shifter_3__5, _8bit_shifter_3__6, _8bit_shifter_3__7, _8bit_shifter_4__0,
       _8bit_shifter_4__1, _8bit_shifter_4__2, _8bit_shifter_4__3, _8bit_shifter_4__4, _8bit_shifter_4__5,
       _8bit_shifter_4__6, _8bit_shifter_4__7, and_1_out, and_2_out, and_3_out, and_4_out, DOWN_out,
       ks_1_ko1, ks_1_ko2, ks_1_ko3, ks_1_ko4, ksmoth_1_ko1, ksmoth_1_ko2, ksmoth_1_ko3, ksmoth_1_ko4,
       LEFT_out, mem_1_d0, mem_1_d1, mem_1_d2, mem_1_d3, not_1_out, not_2_out, not_3_out, not_4_out,
       or_1_out, RIGHT_out, rs_ff_as_1_q, UP_out, Z_out;

  Button LEFT (.out(LEFT_out));
  Button Z (.out(Z_out));
  Button UP (.out(UP_out));
  Button RIGHT (.out(RIGHT_out));
  Button DOWN (.out(DOWN_out));
  RS_FF_AS rs_ff_as_1 (.S(Z_out), .R(or_1_out), .Q(rs_ff_as_1_q));  // open: nQ
  ks ks_1 (
    .KI1(UP_out), .KI2(LEFT_out), .KI3(RIGHT_out), .KI4(DOWN_out), .KO1(ks_1_ko1), .KO2(ks_1_ko2),
    .KO3(ks_1_ko3), .KO4(ks_1_ko4));
  mem mem_1 (.R(rs_ff_as_1_q), .CP(clk), .D0(mem_1_d0), .D1(mem_1_d1), .D2(mem_1_d2), .D3(mem_1_d3));
  or or_1 (or_1_out, and_3_out, and_4_out, and_1_out, and_2_out);
  LED led_1 (.in(_8bit_shifter_1__0));
  LED led_2 (.in(_8bit_shifter_1__1));
  LED led_3 (.in(_8bit_shifter_1__2));
  Ksmoth ksmoth_1 (
    .KI3(ks_1_ko1), .KI4(ks_1_ko2), .KI2(ks_1_ko3), .KI1(ks_1_ko4), .CP(clk), .KO3(ksmoth_1_ko3),
    .KO4(ksmoth_1_ko4), .KO2(ksmoth_1_ko2), .KO1(ksmoth_1_ko1));
  LED led_4 (.in(_8bit_shifter_1__3));
  LED led_5 (.in(_8bit_shifter_1__4));
  LED led_6 (.in(_8bit_shifter_1__5));
  LED led_7 (.in(_8bit_shifter_1__6));
  and and_1 (and_1_out, not_2_out, _8bit_shifter_2__7);
  and and_2 (and_2_out, _8bit_shifter_1__7, not_1_out);
  _8bit_shifter _8bit_shifter_1 (
    .D(mem_1_d1), .MR(rs_ff_as_1_q), .CP(clk), ._7(_8bit_shifter_1__7), ._6(_8bit_shifter_1__6),
    ._5(_8bit_shifter_1__5), ._4(_8bit_shifter_1__4), ._3(_8bit_shifter_1__3), ._2(_8bit_shifter_1__2),
    ._1(_8bit_shifter_1__1), ._0(_8bit_shifter_1__0));
  not not_1 (not_1_out, ksmoth_1_ko4);
  LED led_8 (.in(_8bit_shifter_1__7));
  LED led_9 (.in(ksmoth_1_ko4));
  not not_2 (not_2_out, ksmoth_1_ko1);
  _8bit_shifter _8bit_shifter_2 (
    .D(mem_1_d3), .MR(rs_ff_as_1_q), .CP(clk), ._7(_8bit_shifter_2__7), ._6(_8bit_shifter_2__6),
    ._5(_8bit_shifter_2__5), ._4(_8bit_shifter_2__4), ._3(_8bit_shifter_2__3), ._2(_8bit_shifter_2__2),
    ._1(_8bit_shifter_2__1), ._0(_8bit_shifter_2__0));
  LED led_10 (.in(_8bit_shifter_3__0));
  LED led_11 (.in(_8bit_shifter_3__1));
  LED led_12 (.in(_8bit_shifter_3__2));
  LED led_13 (.in(_8bit_shifter_3__3));
  LED led_14 (.in(_8bit_shifter_3__4));
  LED led_15 (.in(_8bit_shifter_3__5));
  LED led_16 (.in(_8bit_shifter_3__6));
  LED led_17 (.in(_8bit_shifter_3__7));
  LED led_18 (.in(ksmoth_1_ko3));
  LED led_19 (.in(rs_ff_as_1_q));
  LED led_20 (.in(ksmoth_1_ko1));
  LED led_21 (.in(_8bit_shifter_2__7));
  LED led_22 (.in(_8bit_shifter_2__6));
  LED led_23 (.in(_8bit_shifter_2__5));
  LED led_24 (.in(_8bit_shifter_2__4));
  LED led_25 (.in(_8bit_shifter_2__3));
  LED led_26 (.in(_8bit_shifter_2__2));
  LED led_27 (.in(_8bit_shifter_2__1));
  LED led_28 (.in(_8bit_shifter_2__0));
  _8bit_shifter _8bit_shifter_3 (
    .D(mem_1_d0), .MR(rs_ff_as_1_q), .CP(clk), ._7(_8bit_shifter_3__7), ._6(_8bit_shifter_3__6),
    ._5(_8bit_shifter_3__5), ._4(_8bit_shifter_3__4), ._3(_8bit_shifter_3__3), ._2(_8bit_shifter_3__2),
    ._1(_8bit_shifter_3__1), ._0(_8bit_shifter_3__0));
  not not_3 (not_3_out, ksmoth_1_ko3);
  LED led_29 (.in(_8bit_shifter_4__6));
  LED led_30 (.in(_8bit_shifter_4__7));
  LED led_31 (.in(ksmoth_1_ko2));
  not not_4 (not_4_out, ksmoth_1_ko2);
  _8bit_shifter _8bit_shifter_4 (
    .D(mem_1_d2), .MR(rs_ff_as_1_q), .CP(clk), ._7(_8bit_shifter_4__7), ._6(_8bit_shifter_4__6),
    ._5(_8bit_shifter_4__5), ._4(_8bit_shifter_4__4), ._3(_8bit_shifter_4__3), ._2(_8bit_shifter_4__2),
    ._1(_8bit_shifter_4__1), ._0(_8bit_shifter_4__0));
  and and_3 (and_3_out, not_4_out, _8bit_shifter_4__7);
  and and_4 (and_4_out, not_3_out, _8bit_shifter_3__7);
  LED led_32 (.in(_8bit_shifter_4__2));
  LED led_33 (.in(_8bit_shifter_4__3));
  LED led_34 (.in(_8bit_shifter_4__4));
  LED led_35 (.in(_8bit_shifter_4__5));
  LED led_36 (.in(_8bit_shifter_4__0));
  LED led_37 (.in(_8bit_shifter_4__1));

  // Notes on the sheet:
  //   clk: Hz: 4
endmodule
