// Digital circuit ks'.dig as structural Verilog
module ks (
  input  KI1,
  input  KI2,
  input  KI3,
  input  KI4,
  output KO1,
  output KO2,
  output KO3,
  output KO4
);

  wire and_1_out, and_2_out, and_3_out, and_4_out, nor_1_out, nor_3_out, nor_5_out, nor_7_out, or_1_out,
       or_2_out, or_3_out, or_4_out;

  or or_1 (or_1_out, and_2_out, and_3_out, and_4_out);
  or or_2 (or_2_out, and_1_out, and_3_out, and_4_out);
  or or_3 (or_3_out, and_1_out, and_2_out, and_4_out);
  or or_4 (or_4_out, and_1_out, and_2_out, and_3_out);
  nor nor_1 (nor_1_out, KI1, KO1);
  nor nor_2 (KO1, nor_1_out, or_1_out);
  nor nor_3 (nor_3_out, KI2, KO2);
  nor nor_4 (KO2, nor_3_out, or_2_out);
  nor nor_5 (nor_5_out, KI3, KO3);
  nor nor_6 (KO3, nor_5_out, or_3_out);
  nor nor_7 (nor_7_out, KI4, KO4);
  nor nor_8 (KO4, nor_7_out, or_4_out);
  and and_1 (and_1_out, KO1, KI1);
  and and_2 (and_2_out, KO2, KI2);
  and and_3 (and_3_out, KO3, KI3);
  and and_4 (and_4_out, KO4, KI4);
endmodule
