// Digital circuit mem.dig as structural Verilog
module mem (
  input  R,
  input  CP,
  output D0,
  output D1,
  output D2,
  output D3
);

  wire _4bit_counter_1_cp_2, _4bit_counter_2_cp_2, _4bit_counter_3_cp_2;
  wire [3:0] _4bit_counter_1_qd, _4bit_counter_2_qd, _4bit_counter_3_qa, _4bit_counter_4_qa;

  _4bit_counter _4bit_counter_1 (
    .CP(CP), .R(R), .QA(_4bit_counter_1_qd[0]), .QB(_4bit_counter_1_qd[1]), .QC(_4bit_counter_1_qd[2]),
    .QD(_4bit_counter_1_qd[3]), .CP_2(_4bit_counter_1_cp_2));
  _4bit_counter _4bit_counter_2 (
    .CP(_4bit_counter_1_cp_2), .R(R), .QA(_4bit_counter_2_qd[0]), .QB(_4bit_counter_2_qd[1]),
    .QC(_4bit_counter_2_qd[2]), .QD(_4bit_counter_2_qd[3]), .CP_2(_4bit_counter_2_cp_2));
  _4bit_counter _4bit_counter_3 (
    .CP(_4bit_counter_2_cp_2), .R(R), .QA(_4bit_counter_3_qa[0]), .QB(_4bit_counter_3_qa[1]),
    .QC(_4bit_counter_3_qa[2]), .QD(_4bit_counter_3_qa[3]), .CP_2(_4bit_counter_3_cp_2));
  _4bit_counter _4bit_counter_4 (
    .CP(_4bit_counter_3_cp_2), .R(R), .QA(_4bit_counter_4_qa[0]), .QB(_4bit_counter_4_qa[1]),
    .QC(_4bit_counter_4_qa[2]), .QD(_4bit_counter_4_qa[3]));  // open: CP_2
  ROM #(.AddrBits(16), .Bits(4)) rom_1 (
    .A({_4bit_counter_4_qa, _4bit_counter_3_qa, _4bit_counter_2_qd, _4bit_counter_1_qd}), .sel(1'b1),
    .D({D3, D2, D1, D0}));

  // Notes on the sheet:
  //   contents of rom_1 (hex, n*v repeats v):
  //   1,0,1,0,1,0,8,0,2,0,0,0,8,0,0,1,1,0,0,2,0,0,4,0,0,0,8,0,0,0,4,0,1,0,0,8,0,0,4,0,0,
  //   2,0,2
endmodule
